# Fritzing sketch globe_board (saved by Fritzing 0.8.5b)
stripboards: 2

parts:
  U1 = atmega168 [package=dip]
  R1 = Resistor [tolerance=±5% resistance=100 package=THT]
  J4 = female alternating pin header, 2 pins [form="♀ (female)"]
  LED1 = LED - 3mm [color="Infrared (940nm)" package="3 mm [THT]"]
  S2 = Pushbutton [package="[THT]"]
  S3 = Pushbutton [package="[THT]"]
  S4 = Pushbutton [package="[THT]"]
  S5 = Pushbutton [package="[THT]"]
  S6 = Pushbutton [package="[THT]"]
  C1 = Ceramic Capacitor [capacitance=10nF package="100 mil [THT, multilayer]"]
  S7 = Tilt Switch [package=THT]
  C2 = Ceramic Capacitor [capacitance=10nF package="100 mil [THT, multilayer]"]
  D1 = Rectifier Diode [part_number=1N4001 package="300 mil [THT]"]
  D2 = Rectifier Diode [part_number=1N4001 package="300 mil [THT]"]
  D3 = Rectifier Diode [part_number=1N4001 package="300 mil [THT]"]
  D4 = Rectifier Diode [part_number=1N4001 package="300 mil [THT]"]
  D5 = Rectifier Diode [part_number=1N4001 package="300 mil [THT]"]
  VCC1 = Battery
  LED2 = LED - 3mm [color="Red (633nm)" package="3 mm [THT]"]
  R2 = Resistor [tolerance=±5% resistance=100 package=THT]
  D7 = Rectifier Diode [part_number=1N4001 package="300 mil [THT]"]
  R3 = Resistor [tolerance=±5% resistance=10k package=THT]
  S1 = Pushbutton [package="[THT]"]
  U2 = SD_CARD_SOCKET [package=sdcard_4uconn]

nets:
  N1: U1.RESET, R3.Pin_1
  N2: U1.D2, D1.anode, D2.anode, D3.anode, D4.anode, D5.anode, D7.anode
  N3: U1.D3_(PWM), S6.Pin_4, D5.cathode
  N4: U1.D4, D7.cathode, S1.Pin_4
  N5: U1.VCC, R3.Pin_0
  N6: U1.GND#7, S2.Pin_1, S3.Pin_1, S4.Pin_1, S5.Pin_1, S6.Pin_1, C1.0, C2.0, S1.Pin_1, S1.Pin_2
  N7: U1.XLAT1, C1.1, S7.Pin_1
  N8: U1.XLAT2, S7.Pin_2, C2.1
  N9: U1.D5_(PWM), S2.Pin_4, D1.cathode
  N10: U1.D6_(PWM), S3.Pin_3, S3.Pin_4, D2.cathode
  N11: U1.D7, S4.Pin_3, S4.Pin_4, D3.cathode
  N12: U1.D8, S5.Pin_3, S5.Pin_4, D4.cathode
  N13: U1.D9_(PWM), J4.pin2, LED1.anode
  N14: U1.D10_(PWM), U2.VDD
  N15: U1.D11_(PWM), U2.VSS1
  N16: U1.D12, U2.SH
  N17: U1.D13, R2.Pin_0, U2.CMD
  N18: U1.AVCC, U1.AREF, VCC1.+, U2.CLK
  N19: U1.GND#21, R1.Pin_1, VCC1.-, LED2.cathode, U2.CD_DAT3
  N20: R1.Pin_0, J4.pin1, LED1.cathode
  N21: LED2.anode, R2.Pin_1

notes:
  Europe
  Africa
  Asia
  North America
  South America
  Australia
