# Fritzing sketch icsp_board (saved by Fritzing 0.7.10b)
stripboards: 1

parts:
  U3 = atmega168 [package=dip]
  J5 = male pin header, 3 pins [form="♂ (male)"]
  J6 = male pin header, 3 pins [form="♂ (male)"]
  J7 = male pin header, 14 pins [form="♂ (male)"]
  J8 = male pin header, 14 pins [form="♂ (male)"]
  C3 = Ceramic Capacitor [capacitance=10nF package="100 mil [THT, multilayer]"]
  C4 = Ceramic Capacitor [capacitance=10nF package="100 mil [THT, multilayer]"]  # not connected
  XTAL2 = Crystal [frequency="16 Mhz" package=THT]
  R1 = Resistor [tolerance=±5% resistance=220 package=THT]
  S1 = Pushbutton [package="[THT]"]

nets:
  N1: U3.RESET, J5.pin3, J7.pin14, R1.Pin_1, S1.Pin_3, S1.Pin_4
  N2: U3.D0_(RX), J7.pin13
  N3: U3.D1_(TX), J7.pin12
  N4: U3.D2, J7.pin11
  N5: U3.D3_(PWM), J7.pin10
  N6: U3.D4, J7.pin9
  N7: U3.VCC, J7.pin8, R1.Pin_0
  N8: U3.GND#7, J6.pin3, J7.pin7
  N9: U3.XLAT1, J7.pin6, C3.0, XTAL2.pin_1
  N10: U3.XLAT2, J7.pin5, XTAL2.pin_0
  N11: U3.D5_(PWM), J7.pin4
  N12: U3.D6_(PWM), J7.pin3
  N13: U3.D7, J7.pin2
  N14: U3.D8, J7.pin1
  N15: U3.D9_(PWM), J8.pin1
  N16: U3.D10_(PWM), J8.pin2
  N17: U3.D11_(PWM), J6.pin2, J8.pin3
  N18: U3.D12, J5.pin1, J8.pin4
  N19: U3.D13, J5.pin2, J8.pin5
  N20: U3.AVCC, J6.pin1, J8.pin6
  N21: U3.AREF, J8.pin7
  N22: U3.GND#21, J8.pin8, C3.1, S1.Pin_1, S1.Pin_2
  N23: U3.A0, J8.pin9
  N24: U3.A1, J8.pin10
  N25: U3.A2, J8.pin11
  N26: U3.A3, J8.pin12
  N27: U3.A4, J8.pin13
  N28: U3.A5, J8.pin14
