# Fritzing sketch servo_board (saved by Fritzing 0.7.10b)
stripboards: 1

parts:
  J1 = female pin header, 1 pin [form="♀ (female)"]
  J3 = male pin header, 8 pins [form="♂ (male)"]  # not connected
  J2 = male pin header, 8 pins [form="♂ (male)"]
  U1 = atmega168 [package=dip]
  U2 = mystery part, 3 pins [chip_label="IR receiver"]
  J4 = female pin header, 3 pins [form="♀ (female)"]
  Y1 = Resonator [frequency="16 Mhz" package=THT]
  J5 = Basic Servo
  SPKR1 = Loudspeaker
  Q1 = NPN-Transistor [package="TO92 [THT]"]
  J6 = female pin header, 3 pins [form="♀ (female)"]
  J7 = female pin header, 2 pins [form="♀ (female)"]
  R1 = Resistor [tolerance=±5% resistance=15k package=THT]
  LED1 = LED - 3mm [color="Red (633nm)" package="3 mm [THT]"]
  R2 = Resistor [tolerance=±5% resistance=220 package=THT]
  J8 = female pin header, 1 pin [form="♀ (female)"]

nets:
  N1: J1.pin1, J5.vcc, SPKR1.pin2, J6.pin2, J7.pin1, R1.Pin_1, J8.pin1
  N2: J2.pin4, U1.GND#21, R2.Pin_1
  N3: J2.pin6, U1.A5
  N4: J2.pin7, U1.A4
  N5: J2.pin8, U1.AVCC
  N6: U1.D2, U2.pin3, J4.pin3
  N7: U1.D3_(PWM), J5.pulse, J6.pin1
  N8: U1.D4, Q1.B
  N9: U1.VCC, U2.pin1, J4.pin1
  GND: U1.GND#7, U2.pin2, J4.pin2, Y1.GND, J5.gnd, Q1.E, J6.pin3
  N10: U1.XLAT1, Y1.0
  N11: U1.XLAT2, Y1.pin_1
  N12: U1.D13, LED1.anode
  N13: SPKR1.pin1, Q1.C, J7.pin2, R1.Pin_0
  N14: LED1.cathode, R2.Pin_0
